// Digital circuit mode_selector.dig as structural Verilog
module mode_selector (
  input  ID,
  input  PWD,
  input  DIS,
  input  RESET,
  input  CLK,
  input  RST,
  output IDO,
  output PWDO
);

  wire multiplexer_1_out, multiplexer_2_out, not_1_out, or_1_out;

  not not_1 (not_1_out, RST);
  Multiplexer multiplexer_1 (.sel(DIS), .in_0(ID), .in_1(IDO), .out(multiplexer_1_out));
  Multiplexer multiplexer_2 (.sel(DIS), .in_0(PWD), .in_1(PWDO), .out(multiplexer_2_out));
  or or_1 (or_1_out, RESET, not_1_out);
  JK_FF_AS jk_ff_as_1 (
    .Set(1'b0), .J(multiplexer_2_out), .C(CLK), .K(multiplexer_1_out), .Clr(or_1_out), .Q(PWDO), .nQ(IDO));
endmodule
