// Digital circuit shifter_pwd.dig as structural Verilog
module shifter_pwd (
  input  [3:0] DATA_in,
  input  EN,
  input  DA,
  input  CLK,
  input  RST,
  input  [15:0] PWD_in,
  output LED1,
  output LED2,
  output LED3,
  output LED4,
  output MATCH
);

  wire and_1_out, and_2_out, and_3_out, and_4_out, and_5_out, and_7_out, and_8_out, and_9_out, not_1_out,
       not_2_out, or_1_out;
  wire [3:0] d_ff_as_1_q, d_ff_as_2_q, d_ff_as_3_q, d_ff_as_4_q, div_1_r, div_2_r, div_3_r, div_4_r,
       multiplexer_1_out, multiplexer_2_out, multiplexer_3_out, multiplexer_4_out, xnor_1_out, xnor_2_out,
       xnor_3_out, xnor_4_out;
  wire [15:0] div_1_q, div_2_q, div_3_q;
  wire [15:4] div_1_r_2, div_2_r_2, div_3_r_2, div_4_r_2;

  not not_1 (not_1_out, EN);
  not not_2 (not_2_out, RST);
  and and_1 (and_1_out, DA, EN);
  or or_1 (or_1_out, not_1_out, not_2_out);
  Div #(.Bits(16)) div_1 (.a(PWD_in), .b(16'ha), .q(div_1_q), .r({div_1_r_2, div_1_r}));
  Div #(.Bits(16)) div_2 (.a(div_1_q), .b(16'ha), .q(div_2_q), .r({div_2_r_2, div_2_r}));
  Div #(.Bits(16)) div_3 (.a(div_2_q), .b(16'ha), .q(div_3_q), .r({div_3_r_2, div_3_r}));
  Div #(.Bits(16)) div_4 (.a(div_3_q), .b(16'ha), .r({div_4_r_2, div_4_r}));  // open: q
  D_FF_AS #(.Bits(4)) d_ff_as_1 (
    .Set(1'b0), .D(multiplexer_1_out), .C(CLK), .Clr(or_1_out), .Q(d_ff_as_1_q));  // open: nQ
  Multiplexer #(.Bits(4)) multiplexer_1 (.sel(and_1_out), .in_0(d_ff_as_1_q), .in_1(DATA_in), .out(multiplexer_1_out));
  assign xnor_1_out = ~(d_ff_as_1_q ^ div_1_r);  // XNOr xnor_1, 4 bits wide
  assign xnor_2_out = ~(d_ff_as_2_q ^ div_2_r);  // XNOr xnor_2, 4 bits wide
  assign xnor_3_out = ~(d_ff_as_3_q ^ div_3_r);  // XNOr xnor_3, 4 bits wide
  assign xnor_4_out = ~(d_ff_as_4_q ^ div_4_r);  // XNOr xnor_4, 4 bits wide
  D_FF_AS #(.Bits(4)) d_ff_as_2 (
    .Set(1'b0), .D(multiplexer_2_out), .C(CLK), .Clr(or_1_out), .Q(d_ff_as_2_q));  // open: nQ
  Multiplexer #(.Bits(4)) multiplexer_2 (
    .sel(and_1_out), .in_0(d_ff_as_2_q), .in_1(d_ff_as_1_q), .out(multiplexer_2_out));
  Multiplexer #(.Bits(4)) multiplexer_3 (
    .sel(and_1_out), .in_0(d_ff_as_3_q), .in_1(d_ff_as_2_q), .out(multiplexer_3_out));
  and and_2 (and_2_out, xnor_1_out[0], xnor_1_out[1], xnor_1_out[2], xnor_1_out[3]);
  and and_3 (and_3_out, xnor_2_out[0], xnor_2_out[1], xnor_2_out[2], xnor_2_out[3]);
  and and_4 (and_4_out, xnor_3_out[0], xnor_3_out[1], xnor_3_out[2], xnor_3_out[3]);
  and and_5 (and_5_out, xnor_4_out[0], xnor_4_out[1], xnor_4_out[2], xnor_4_out[3]);
  D_FF_AS #(.Bits(4)) d_ff_as_3 (
    .Set(1'b0), .D(multiplexer_3_out), .C(CLK), .Clr(or_1_out), .Q(d_ff_as_3_q));  // open: nQ
  D_FF_AS #(.Bits(4)) d_ff_as_4 (
    .Set(1'b0), .D(multiplexer_4_out), .C(CLK), .Clr(or_1_out), .Q(d_ff_as_4_q));  // open: nQ
  Multiplexer #(.Bits(4)) multiplexer_4 (
    .sel(and_1_out), .in_0(d_ff_as_4_q), .in_1(d_ff_as_3_q), .out(multiplexer_4_out));
  and and_6 (MATCH, LED4, and_2_out, and_3_out, and_4_out, and_5_out);
  JK_FF_AS jk_ff_as_1 (.Set(1'b0), .J(and_1_out), .C(CLK), .K(1'b0), .Clr(or_1_out), .Q(LED1));  // open: nQ
  JK_FF_AS jk_ff_as_2 (.Set(1'b0), .J(and_7_out), .C(CLK), .K(1'b0), .Clr(or_1_out), .Q(LED2));  // open: nQ
  JK_FF_AS jk_ff_as_3 (.Set(1'b0), .J(and_8_out), .C(CLK), .K(1'b0), .Clr(or_1_out), .Q(LED3));  // open: nQ
  JK_FF_AS jk_ff_as_4 (.Set(1'b0), .J(and_9_out), .C(CLK), .K(1'b0), .Clr(or_1_out), .Q(LED4));  // open: nQ
  and and_7 (and_7_out, LED1, and_1_out);
  and and_8 (and_8_out, LED2, and_1_out);
  and and_9 (and_9_out, LED3, and_1_out);
endmodule
