// Digital circuit timer.dig as structural Verilog
module timer (
  input  START,
  input  CLK,
  input  RST,
  output RESET,
  output DIS
);

  wire and_6_out, and_7_out, d_ff_as_1_nq, d_ff_as_1_q, d_ff_as_2_nq, d_ff_as_2_q, d_ff_as_3_nq, d_ff_as_3_q,
       d_ff_as_4_nq, d_ff_as_4_q, d_ff_as_5_nq, d_ff_as_5_q, d_ff_as_6_nq, d_ff_as_6_q, multiplexer_1_out,
       multiplexer_2_out, multiplexer_3_out, multiplexer_4_out, multiplexer_5_out, not_1_out, not_2_out,
       not_3_out, not_4_out, or_1_out;
  wire [0:0] and_1_out, and_2_out, and_3_out;
  wire [1:0] and_5_out;

  and and_1 (and_1_out[0], DIS, START);
  not not_1 (not_1_out, RST);
  or or_1 (or_1_out, not_1_out, RESET);
  and and_2 (and_2_out[0], d_ff_as_1_q, and_1_out[0]);
  and and_3 (and_3_out[0], d_ff_as_2_q, and_2_out[0]);
  and and_4 (and_5_out[0], d_ff_as_3_q, and_3_out[0]);
  Multiplexer #(.Selector_Bits(2)) multiplexer_1 (
    .sel({and_5_out[1], and_1_out[0]}), .in_0(d_ff_as_1_q), .in_1(d_ff_as_1_nq), .in_2(1'b0), .in_3(1'b0),
    .out(multiplexer_1_out));
  Multiplexer #(.Selector_Bits(2)) multiplexer_2 (
    .sel({and_5_out[1], and_2_out[0]}), .in_0(d_ff_as_2_q), .in_1(d_ff_as_2_nq), .in_2(1'b0), .in_3(1'b0),
    .out(multiplexer_2_out));
  Multiplexer #(.Selector_Bits(2)) multiplexer_3 (
    .sel({and_5_out[1], and_3_out[0]}), .in_0(d_ff_as_3_q), .in_1(d_ff_as_3_nq), .in_2(1'b0), .in_3(1'b0),
    .out(multiplexer_3_out));
  Multiplexer #(.Selector_Bits(2)) multiplexer_4 (
    .sel(and_5_out), .in_0(d_ff_as_4_q), .in_1(d_ff_as_4_nq), .in_2(1'b0), .in_3(1'b0),
    .out(multiplexer_4_out));
  D_FF_AS d_ff_as_1 (.Set(1'b0), .D(multiplexer_1_out), .C(CLK), .Clr(or_1_out), .Q(d_ff_as_1_q), .nQ(d_ff_as_1_nq));
  D_FF_AS d_ff_as_2 (.Set(1'b0), .D(multiplexer_2_out), .C(CLK), .Clr(or_1_out), .Q(d_ff_as_2_q), .nQ(d_ff_as_2_nq));
  D_FF_AS d_ff_as_3 (.Set(1'b0), .D(multiplexer_3_out), .C(CLK), .Clr(or_1_out), .Q(d_ff_as_3_q), .nQ(d_ff_as_3_nq));
  D_FF_AS d_ff_as_4 (.Set(1'b0), .D(multiplexer_4_out), .C(CLK), .Clr(or_1_out), .Q(d_ff_as_4_q), .nQ(d_ff_as_4_nq));
  not not_2 (not_2_out, d_ff_as_2_q);
  not not_3 (not_3_out, d_ff_as_3_q);
  and and_5 (and_5_out[1], d_ff_as_1_q, not_2_out, not_3_out, d_ff_as_4_q);
  not not_4 (not_4_out, RESET);
  and and_6 (and_6_out, d_ff_as_5_nq, not_4_out);
  and and_7 (and_7_out, multiplexer_5_out, not_4_out);
  D_FF_AS d_ff_as_5 (.Set(1'b0), .D(and_6_out), .C(and_5_out[1]), .Clr(or_1_out), .Q(d_ff_as_5_q), .nQ(d_ff_as_5_nq));
  D_FF_AS d_ff_as_6 (.Set(1'b0), .D(and_7_out), .C(and_5_out[1]), .Clr(or_1_out), .Q(d_ff_as_6_q), .nQ(d_ff_as_6_nq));
  Multiplexer multiplexer_5 (.sel(d_ff_as_5_q), .in_0(d_ff_as_6_q), .in_1(d_ff_as_6_nq), .out(multiplexer_5_out));
  and and_8 (RESET, d_ff_as_5_q, d_ff_as_6_q);
  and and_9 (DIS, START, ~RESET);  // And
endmodule
